// Logisim project Ejercicio1.circ as structural Verilog: 1 circuit, main circuit main
module main (
  input  in_1,
  input  in_2,
  input  in_3
);

  wire and_1_out, and_2_out, and_5_out, and_6_out, B, B2, B3, nor_1_out, nor_2_out, nor_3_out, nor_4_out,
       nor_5_out, nor_6_out, not_1_out, not_2_out, not_3_out, not_4_out, not_5_out, not_6_out, not_7_out,
       not_8_out, not_9_out, not_10_out, not_11_out, or_1_out, or_2_out, or_3_out, P, S, S1, S2;

  Button button_1 (.out(B3));
  Button button_2 (.out(S2));
  Button button_3 (.out(B2));
  Button button_4 (.out(S1));
  not not_1 (not_1_out, in_3);
  not not_2 (not_2_out, in_2);
  not not_3 (not_3_out, in_1);
  nor nor_1 (nor_1_out, B3, S2, B2, S1);
  nor nor_2 (nor_2_out, in_1, in_2, not_1_out);
  nor nor_3 (nor_3_out, in_1, not_2_out, in_3);
  nor nor_4 (nor_4_out, not_3_out, in_2, in_3);
  nor nor_5 (nor_5_out, S1, S2, in_3);
  not not_4 (not_4_out, B3);
  not not_5 (not_5_out, in_1);
  not not_6 (not_6_out, B2);
  not not_7 (not_7_out, in_2);
  or or_1 (or_1_out, nor_2_out, nor_3_out, nor_4_out);
  and and_1 (and_1_out, not_4_out, B2, in_2, not_5_out);
  and and_2 (and_2_out, not_6_out, in_1, B3, not_7_out);
  and and_3 (P, nor_1_out, or_1_out);
  and and_4 (B, nor_5_out, or_2_out);
  or or_2 (or_2_out, and_1_out, and_2_out);
  _7_Segment_Display u_7_segment_display_1 (.g(S), .f(S), .a(S), .d(S), .c(S));  // open: b, e, dp
  _7_Segment_Display u_7_segment_display_2 (.g(P), .f(P), .a(P), .b(P), .e(P));  // open: d, c, dp
  _7_Segment_Display u_7_segment_display_3 (.g(B), .f(B), .e(B), .d(B), .c(B));  // open: a, b, dp
  not not_8 (not_8_out, S1);
  not not_9 (not_9_out, S2);
  not not_10 (not_10_out, in_2);
  not not_11 (not_11_out, in_3);
  nor nor_6 (nor_6_out, B3, B2, in_1);
  and and_5 (and_5_out, not_8_out, S2, in_2, not_11_out);
  and and_6 (and_6_out, not_9_out, in_3, not_10_out, S1);
  or or_3 (or_3_out, and_5_out, and_6_out);
  and and_7 (S, nor_6_out, or_3_out);

  // Other names for the same wires on the sheet: P1 = in_3; P2 = in_2; P3 = in_1
endmodule
